# Fritzing sketch Servo-joystick (saved by Fritzing 0.9.3b)
circuit board: 8.46667cm x 5.64444cm
breadboards: 1

parts:
  Componente2 = Arduino Mega 2560 (Rev3)
  J1 = Basic Servo
  J2 = Basic Servo
  Componente1 = Adafruit Analog 2-Axis Joystick [part_number="Adafruit #512"]

nets:
  N1: Componente2.A4, Componente1.XOUT
  N2: Componente2.A5, Componente1.YOUT
  GND: Componente2.GND, J1.gnd, J2.gnd, Componente1.GND
  N3: Componente2.D8_PWM, J1.pulse
  VCC: Componente2.5V, J1.vcc, J2.vcc, Componente1.VCC
  N4: Componente2.D7_PWM, J2.pulse

notes:
  Eje X
  Eje Y

custom parts:
  Adafruit Analog 2-Axis Joystick: This mini-kit makes it easy to mount a PSP/Xbox-like thumb joystick to your project. The thumbstick is an analog joystick - more accurate and sensitive than just 'directional' joysticks - with a 'press in to select' button. Since it's analog, you'll need two analog reading pins on your microcontroller to determine X and Y. Having an extra digital input will let you read the switch. The pack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
